# Fritzing sketch wiring_diagram (saved by Fritzing 0.9.3b)
breadboards: 1

parts:
  Raspberry_Pi_1 = Raspberry Pi 3 [part_number=RPI-3-V1.2]
  M2 = Stepper Motor - Bipolar
  Power_plug1 = Power plug
  M1 = Stepper Motor - Bipolar
  C12 = Electrolytic Capacitor [capacitance=1000μF package="1010 [SMD, electrolytic]"]
  C13 = Electrolytic Capacitor [capacitance=1000μF package="1010 [SMD, electrolytic]"]
  Pololu_A6 = Pololu A4988 [package=SO16]
  Pololu_A7 = Pololu A4988 [package=SO16]

nets:
  N1: Raspberry_Pi_1.GPIO13, Pololu_A6.STEP
  N2: Raspberry_Pi_1.GPIO26, Pololu_A6.DIR
  N3: Raspberry_Pi_1.GPIO21, Pololu_A7.DIR
  N4: Raspberry_Pi_1.GPIO16, Pololu_A7.STEP
  N5: Raspberry_Pi_1.GND, Pololu_A6.GND#8, Pololu_A7.GND#8
  VDD: Raspberry_Pi_1.5V, Pololu_A6.VDD, Pololu_A7.VDD
  N6: M2.A, Pololu_A7.2B
  N7: M2.C, Pololu_A7.2A
  N8: M2.B, Pololu_A7.1A
  N9: M2.D, Pololu_A7.1B
  N10: Power_plug1.GND, C12.-, C13.-, Pololu_A6.GND#14, Pololu_A7.GND#14
  N11: Power_plug1.VCC, C12.+, C13.+, Pololu_A6.VMOT, Pololu_A7.VMOT
  N12: M1.A, Pololu_A6.2B
  N13: M1.C, Pololu_A6.2A
  N14: M1.B, Pololu_A6.1A
  N15: M1.D, Pololu_A6.1B
  N16: Pololu_A6.RESET, Pololu_A6.SLEEP
  N17: Pololu_A7.RESET, Pololu_A7.SLEEP

notes:
  Motor Power Supply
  12V - 2A
  Decoupling capacitors
  100 uF
  Logic Power Supply
  3 - 5V
  Pan motor
  Tilt motor

custom parts:
  Pololu A4988: The A4988 stepper motor driver carrier is a breakout board for Allegro’s A4988 microstepping bipolar stepper motor driver. The driver features adjustable current limiting, overcurrent and overtemperature protection, and five different microstep resolutions (down to 1/16-step). It operates from 8 – 35 V and can deliver up to approximately 1 A per phase without a heat sink or forced air flow (it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
